# Fritzing sketch circuit (saved by Fritzing 0.9.3b)
breadboards: 1

parts:
  U1 = NodeMCU V1.0
  Componente1 = Matrix LED de 8x8 basada en MAX7219
  Componente2 = Matrix LED de 8x8 basada en MAX7219
  Componente3 = Matrix LED de 8x8 basada en MAX7219
  Componente4 = Matrix LED de 8x8 basada en MAX7219

nets:
  N1: U1.D6, Componente1.DIN
  N2: U1.D7, Componente1.CLK
  N3: U1.D8, Componente1.CS
  N4: U1.RSV#40, Componente1.VCC
  N5: U1.RSV#41, Componente1.GND#1
  N6: Componente1.VCC(OUT), Componente2.VCC
  N7: Componente1.GND#6, Componente2.GND#1
  N8: Componente1.CS(OUT), Componente2.CS
  N9: Componente1.CLK(OUT), Componente2.CLK
  N10: Componente1.DOUT, Componente2.DIN
  N11: Componente2.VCC(OUT), Componente3.VCC
  N12: Componente2.GND#6, Componente3.GND#1
  N13: Componente2.CS(OUT), Componente3.CS
  N14: Componente2.CLK(OUT), Componente3.CLK
  N15: Componente2.DOUT, Componente3.DIN
  N16: Componente3.VCC(OUT), Componente4.VCC
  N17: Componente3.GND#6, Componente4.GND
  N18: Componente3.CS(OUT), Componente4.CS
  N19: Componente3.CLK(OUT), Componente4.CLK
  N20: Componente3.DOUT, Componente4.DIN

custom parts:
  NodeMCU V1.0: ESP8266 based NodeMCU
